// Logisim project CPU.circ as structural Verilog: 53 circuits, main circuit main
module main (
  input  RAM_A_WE,
  input  RAM_A_OE,
  input  RAM_B_OE,
  input  RAM_B_WE,
  input  INS_RAM_OE,
  input  INS_RAM_WE,
  input  SYS_RAM_OE,
  input  SYS_RAM_WE,
  input  MBR_B_WE,
  input  MBR_A_WE,
  input  MBR_Z_WE,
  input  Flag_WE,
  input  MBR_B_CB,
  input  MBR_A_CB,
  input  MBR_Z_CB,
  input  MAR_Z_WE,
  input  MAR_A_WE,
  input  MAR_B_WE,
  input  Reg_8_WE,
  input  Reg_4_WE,
  input  Reg_2_WE,
  input  Reg_6_WE,
  input  Reg_7_WE,
  input  Reg_5_WE,
  input  Reg_3_WE,
  input  Reg_1_WE,
  input  Bus_Select_Bit0,
  input  Bus_Select_Bit1,
  input  ALU_Out_CB,
  input  Bus_Select_OE,
  input  MAR_A_TO_B,
  input  CC_Reset,
  input  Opcode_WE,
  input  Opcode_Init_CB,
  input  ALU_WE,
  input  MAR_A_TO_Z,
  input  PC_Increment,
  input  MBR_Swap,
  input  Block_Sel_OE,
  input  Block_Count_Inc,
  input  Terminal_WE,
  input  MAR_B_TO_Z,
  input  SYS_RAM_CB,
  input  INS_RAM_CB,
  input  RAM_A_CB,
  input  RAM_B_CB,
  input  Delay_WE,
  input  Reg_Sel_OE
);

  wire alu_1_overflow, and_1_out, and_2_out, and_3_out, and_4_out, and_5_out, and_6_out, and_7_out,
       and_8_out, Block_Selector_b00, Block_Selector_b01, Block_Selector_b10, Block_Selector_b11,
       bus_select_styled_1_r_a, bus_select_styled_1_r_b, bus_select_styled_1_r_ins,
       bus_select_styled_1_r_sys, clock_1_out, Clock_Counter_CC_carry, cmp_4bit_styled_1_eq,
       cmp_5bit_styled_1_eq, delayer_1_clock_out, Flag_q, ins_decoder_1_block_load,
       ins_decoder_1_block_store, ins_decoder_1_halt, ins_decoder_1_mat_mult, ins_decoder_1_move,
       ins_decoder_1_reg_swap, ins_split_1_flag, matmult_1_overflow, nand_1_out, nor_1_out, nor_2_out,
       not_1_out, not_2_out, not_3_out, not_4_out, not_5_out, not_6_out, or_1_out, or_2_out, or_3_out,
       or_4_out, or_5_out, or_6_out, or_7_out, or_8_out, or_9_out, or_10_out, or_11_out, or_12_out,
       or_13_out, or_14_out, or_15_out, or_16_out, or_17_out, or_18_out, or_19_out, or_20_out, or_21_out,
       or_22_out, or_23_out, or_24_out, or_25_out, or_26_out, or_27_out, or_28_out, or_29_out, or_30_out,
       or_31_out, or_32_out, or_33_out, or_34_out, or_35_out, or_36_out, or_37_out, or_38_out, or_39_out,
       or_40_out, or_41_out, or_42_out, or_43_out, or_44_out, or_45_out, or_46_out, or_47_out, or_48_out,
       PC_Max_q, Program_Counter_PC_carry, ram_we_styled_1_a, ram_we_styled_2_a, ram_we_styled_3_b,
       reg_we_styled_1_out_4, reg_we_styled_2_out_4, reg_we_styled_3_out_4, reg_we_styled_4_out_4,
       reg_we_styled_5_out_4, reg_we_styled_6_out_4, reg_we_styled_7_out_4, reg_we_styled_8_out_4,
       register_5_q, register_6_q, register_7_q, register_8_q, register_selector_1_reg1,
       register_selector_1_reg2, register_selector_1_reg3, register_selector_1_reg4,
       register_selector_2_reg5, register_selector_2_reg6, register_selector_2_reg7,
       register_selector_2_reg8, undriven;
  wire [1:0] Block_Count_q;
  wire [3:0] bit_extender_2_out, MBR_A_q, MBR_A_q_2, MBR_A_q_3, MBR_A_q_4, MBR_B_q, MBR_B_q_2, MBR_B_q_3,
       MBR_B_q_4;
  wire [4:0] controlled_buffer_1_out, controlled_buffer_6_out, controlled_buffer_9_out, Delay_q,
       ins_split_1_address_a, ins_split_1_address_b, ins_split_1_opcode, MAR_A_q, MAR_B_q, MAR_Z_q,
       Program_Counter_PC_q;
  wire [4:4] Opcode_q;
  wire [7:0] bit_extender_1_out, Clock_Counter_CC_q;
  wire [15:0] alu_1_result, bit_extender_3_out, bit_extender_4_out, bit_extender_5_out, bit_extender_6_out,
       bit_extender_7_out, controlled_buffer_3_out, controlled_buffer_12_out, controlled_buffer_16_out,
       controlled_buffer_17_out, controlled_buffer_24_out, controlled_buffer_26_out,
       controlled_buffer_27_out, controlled_buffer_28_out, controlled_buffer_31_out,
       controlled_buffer_32_out, controlled_buffer_33_out, controlled_buffer_34_out,
       controlled_buffer_39_out, Instruction_RAM_dout, matmult_1_result, MBR_Z_q, RAM_A_dout, RAM_B_dout,
       Reg1_q, Reg2_q, Reg3_q, Reg4_q, Reg5_q, Reg6_q, Reg7_q, Reg8_q, register_1_q, register_2_q,
       register_3_q, register_4_q, System_RAM_dout, Terminal_q;
  wire [47:0] Control_Unit_CU_data;

  Clock clock_1 (.out(clock_1_out));
  Delayer delayer_1 (.Clock(clock_1_out), .Delay(Delay_q), .Clock_Out(delayer_1_clock_out));
  Counter #(.max('hf), .width(4)) Clock_Counter_CC (
    .load(or_32_out), .up(1'b1), .clk(and_1_out), .D(4'b0000), .carry(Clock_Counter_CC_carry),
    .Q(Clock_Counter_CC_q[3:0]));  // open: clr, count
  ROM #(.dataWidth(48), .misaligned("true")) Control_Unit_CU (.addr(Clock_Counter_CC_q), .data(Control_Unit_CU_data));
  and and_1 (and_1_out, delayer_1_clock_out, nand_1_out, not_2_out);
  or or_1 (or_1_out, RAM_A_WE, Control_Unit_CU_data[0]);
  or or_2 (or_2_out, RAM_A_OE, Control_Unit_CU_data[1]);
  or or_3 (or_3_out, RAM_B_OE, Control_Unit_CU_data[2]);
  or or_4 (or_4_out, RAM_B_WE, Control_Unit_CU_data[3]);
  or or_5 (or_5_out, INS_RAM_OE, Control_Unit_CU_data[4]);
  or or_6 (or_6_out, INS_RAM_WE, Control_Unit_CU_data[5]);
  or or_7 (or_7_out, SYS_RAM_OE, Control_Unit_CU_data[6]);
  or or_8 (or_8_out, SYS_RAM_WE, Control_Unit_CU_data[7]);
  or or_9 (or_9_out, MBR_B_WE, Control_Unit_CU_data[8]);
  or or_10 (or_10_out, MBR_A_WE, Control_Unit_CU_data[9]);
  or or_11 (or_11_out, MBR_Z_WE, Control_Unit_CU_data[10]);
  or or_12 (or_12_out, Flag_WE, Control_Unit_CU_data[11]);
  or or_13 (or_13_out, MBR_B_CB, Control_Unit_CU_data[12]);
  or or_14 (or_14_out, MBR_A_CB, Control_Unit_CU_data[13]);
  or or_15 (or_15_out, MBR_Z_CB, Control_Unit_CU_data[14]);
  or or_16 (or_16_out, MAR_Z_WE, Control_Unit_CU_data[15]);
  or or_17 (or_17_out, MAR_A_WE, Control_Unit_CU_data[16]);
  or or_18 (or_18_out, MAR_B_WE, Control_Unit_CU_data[17]);
  or or_19 (or_19_out, Reg_8_WE, Control_Unit_CU_data[18]);
  or or_20 (or_20_out, Reg_4_WE, Control_Unit_CU_data[19]);
  or or_21 (or_21_out, Reg_2_WE, Control_Unit_CU_data[20]);
  or or_22 (or_22_out, Reg_6_WE, Control_Unit_CU_data[21]);
  or or_23 (or_23_out, Reg_7_WE, Control_Unit_CU_data[22]);
  or or_24 (or_24_out, Reg_5_WE, Control_Unit_CU_data[23]);
  or or_25 (or_25_out, Reg_3_WE, Control_Unit_CU_data[24]);
  or or_26 (or_26_out, Reg_1_WE, Control_Unit_CU_data[25]);
  or or_27 (or_27_out, Bus_Select_Bit0, Control_Unit_CU_data[26]);
  or or_28 (or_28_out, Bus_Select_Bit1, Control_Unit_CU_data[27]);
  or or_29 (or_29_out, ALU_Out_CB, Control_Unit_CU_data[28]);
  or or_30 (or_30_out, Bus_Select_OE, Control_Unit_CU_data[29]);
  or or_31 (or_31_out, MAR_A_TO_B, Control_Unit_CU_data[30]);
  or or_32 (or_32_out, CC_Reset, Control_Unit_CU_data[31]);
  or or_33 (or_33_out, Opcode_WE, Control_Unit_CU_data[32]);
  or or_34 (or_34_out, Opcode_Init_CB, Control_Unit_CU_data[33]);
  or or_35 (or_35_out, ALU_WE, Control_Unit_CU_data[34]);
  or or_36 (or_36_out, MAR_A_TO_Z, Control_Unit_CU_data[35]);
  or or_37 (or_37_out, PC_Increment, Control_Unit_CU_data[36]);
  or or_38 (or_38_out, MBR_Swap, Control_Unit_CU_data[37]);
  or or_39 (or_39_out, Block_Sel_OE, Control_Unit_CU_data[38]);
  or or_40 (or_40_out, Block_Count_Inc, Control_Unit_CU_data[39]);
  or or_41 (or_41_out, Terminal_WE, Control_Unit_CU_data[40]);
  or or_42 (or_42_out, MAR_B_TO_Z, Control_Unit_CU_data[41]);
  or or_43 (or_43_out, SYS_RAM_CB, Control_Unit_CU_data[42]);
  or or_44 (or_44_out, INS_RAM_CB, Control_Unit_CU_data[43]);
  or or_45 (or_45_out, RAM_A_CB, Control_Unit_CU_data[44]);
  or or_46 (or_46_out, RAM_B_CB, Control_Unit_CU_data[45]);
  or or_47 (or_47_out, Delay_WE, Control_Unit_CU_data[46]);
  or or_48 (or_48_out, Reg_Sel_OE, Control_Unit_CU_data[47]);
  nand nand_1 (nand_1_out, cmp_4bit_styled_1_eq, and_2_out);
  CMP_4Bit_Styled cmp_4bit_styled_1 (
    .A(4'b0000), .B(Clock_Counter_CC_q[3:0]), .EQ(cmp_4bit_styled_1_eq));  // open: LT, GT
  nor nor_1 (nor_1_out, Clock_Counter_CC_carry, or_37_out);
  Register #(.width(5)) Delay (.D(MAR_A_q), .en(or_47_out), .clk(and_1_out), .Q(Delay_q));  // open: clr
  Counter #(.max('h1f), .width(5)) Program_Counter_PC (
    .up(1'b1), .count(1'b1), .clk(nor_1_out), .carry(Program_Counter_PC_carry), .Q(Program_Counter_PC_q));  // open: clr, load, D
  INS_SPLIT ins_split_1 (
    .Instruction(controlled_buffer_26_out), .Flag(ins_split_1_flag), .Opcode(ins_split_1_opcode),
    .Address_A(ins_split_1_address_a), .Address_B(ins_split_1_address_b));
  assign controlled_buffer_1_out = not_1_out ? ins_split_1_opcode : 5'bz;  // Controlled_Buffer controlled_buffer_1
  not not_1 (not_1_out, or_34_out);
  Register #(.width(1)) Flag (.D(ins_split_1_flag), .en(or_12_out), .clk(and_1_out), .Q(Flag_q));  // open: clr
  Register #(.width(5)) Opcode (
    .D(controlled_buffer_1_out), .en(or_33_out), .clk(and_1_out), .Q({Opcode_q[4], Clock_Counter_CC_q[7:4]}));  // open: clr
  assign controlled_buffer_1_out = or_34_out ? {5{1'b0}} : 5'bz;  // Controlled_Buffer controlled_buffer_2
  Register_Selector register_selector_1 (
    .OE(or_48_out), .N(MAR_A_q), .Reg1(register_selector_1_reg1), .Reg2(register_selector_1_reg2),
    .Reg3(register_selector_1_reg3), .Reg4(register_selector_1_reg4));  // open: Reg5, Reg6, Reg7, Reg8
  Register #(.width(1)) PC_Max (
    .D(Program_Counter_PC_carry), .en(Program_Counter_PC_carry), .clk(and_1_out), .Q(PC_Max_q));  // open: clr
  CMP_5Bit_Styled cmp_5bit_styled_1 (
    .A(5'b00001), .B(Program_Counter_PC_q), .EQ(cmp_5bit_styled_1_eq));  // open: LT, GT
  Hex_Digit_Display #(.decimalPoint("false")) hex_digit_display_1 (.value(bit_extender_1_out[7:4]));
  assign bit_extender_1_out = {{3{1'b0}}, Program_Counter_PC_q};  // Bit_Extender bit_extender_1
  INS_Decoder ins_decoder_1 (
    .Flag(Flag_q), .Opcode({Opcode_q[4], Clock_Counter_CC_q[7:4]}), .Reg_Swap(ins_decoder_1_reg_swap),
    .Block_Load(ins_decoder_1_block_load), .Block_Store(ins_decoder_1_block_store),
    .Mat_Mult(ins_decoder_1_mat_mult), .Move(ins_decoder_1_move), .Halt(ins_decoder_1_halt));
  not not_2 (not_2_out, ins_decoder_1_halt);
  Reg_WE_Styled reg_we_styled_1 (
    .Ins(ins_decoder_1_reg_swap), .WE(or_24_out), .Sel(register_selector_1_reg1),
    .out_4(reg_we_styled_1_out_4));
  Reg_WE_Styled reg_we_styled_2 (
    .Ins(ins_decoder_1_reg_swap), .WE(or_22_out), .Sel(register_selector_1_reg2),
    .out_4(reg_we_styled_2_out_4));
  and and_2 (and_2_out, not_3_out, cmp_5bit_styled_1_eq, PC_Max_q);
  not not_3 (not_3_out, Program_Counter_PC_carry);
  Hex_Digit_Display #(.decimalPoint("false")) hex_digit_display_2 (.value(bit_extender_1_out[3:0]));
  and and_3 (and_3_out, ins_decoder_1_block_store, or_40_out);
  Register #(.width(16)) Reg1 (
    .D(controlled_buffer_27_out), .en(reg_we_styled_1_out_4), .clk(and_1_out), .Q(Reg1_q));  // open: clr
  Register #(.width(16)) Reg2 (
    .D(controlled_buffer_27_out), .en(reg_we_styled_2_out_4), .clk(and_1_out), .Q(Reg2_q));  // open: clr
  Register #(.width(16)) Reg3 (
    .D(controlled_buffer_27_out), .en(reg_we_styled_3_out_4), .clk(and_1_out), .Q(Reg3_q));  // open: clr
  Reg_WE_Styled reg_we_styled_3 (
    .Ins(ins_decoder_1_reg_swap), .WE(or_23_out), .Sel(register_selector_1_reg3),
    .out_4(reg_we_styled_3_out_4));
  Register #(.width(16)) Reg4 (
    .D(controlled_buffer_27_out), .en(reg_we_styled_4_out_4), .clk(and_1_out), .Q(Reg4_q));  // open: clr
  Reg_WE_Styled reg_we_styled_4 (
    .Ins(ins_decoder_1_reg_swap), .WE(or_19_out), .Sel(register_selector_1_reg4),
    .out_4(reg_we_styled_4_out_4));
  Hex_Digit_Display #(.decimalPoint("false")) hex_digit_display_3 (.value(Clock_Counter_CC_q[7:4]));
  Hex_Digit_Display #(.decimalPoint("false")) hex_digit_display_4 (.value(Clock_Counter_CC_q[3:0]));
  and and_4 (and_4_out, ins_decoder_1_block_load, or_40_out);
  assign controlled_buffer_3_out = register_selector_1_reg1 ? Reg1_q : 16'bz;  // Controlled_Buffer controlled_buffer_3
  assign controlled_buffer_3_out = register_selector_1_reg2 ? Reg2_q : 16'bz;  // Controlled_Buffer controlled_buffer_4
  assign controlled_buffer_3_out = register_selector_1_reg3 ? Reg3_q : 16'bz;  // Controlled_Buffer controlled_buffer_5
  assign controlled_buffer_6_out = or_31_out ? MAR_A_q : 5'bz;  // Controlled_Buffer controlled_buffer_6
  assign controlled_buffer_3_out = register_selector_1_reg4 ? Reg4_q : 16'bz;  // Controlled_Buffer controlled_buffer_7
  assign controlled_buffer_6_out = not_4_out ? ins_split_1_address_b : 5'bz;  // Controlled_Buffer controlled_buffer_8
  not not_4 (not_4_out, or_31_out);
  Register_Selector register_selector_2 (
    .OE(or_48_out), .N(MAR_B_q), .Reg5(register_selector_2_reg5), .Reg6(register_selector_2_reg6),
    .Reg7(register_selector_2_reg7), .Reg8(register_selector_2_reg8));  // open: Reg1, Reg2, Reg3, Reg4
  assign controlled_buffer_9_out = nor_2_out ? Program_Counter_PC_q : 5'bz;  // Controlled_Buffer controlled_buffer_9
  nor nor_2 (nor_2_out, or_42_out, or_36_out);
  assign controlled_buffer_9_out = or_36_out ? MAR_A_q : 5'bz;  // Controlled_Buffer controlled_buffer_10
  Reg_WE_Styled reg_we_styled_5 (
    .Ins(ins_decoder_1_reg_swap), .WE(or_26_out), .Sel(register_selector_2_reg5),
    .out_4(reg_we_styled_5_out_4));
  Reg_WE_Styled reg_we_styled_6 (
    .Ins(ins_decoder_1_reg_swap), .WE(or_21_out), .Sel(register_selector_2_reg6),
    .out_4(reg_we_styled_6_out_4));
  Reg_WE_Styled reg_we_styled_7 (
    .Ins(ins_decoder_1_reg_swap), .WE(or_25_out), .Sel(register_selector_2_reg7),
    .out_4(reg_we_styled_7_out_4));
  Reg_WE_Styled reg_we_styled_8 (
    .Ins(ins_decoder_1_reg_swap), .WE(or_20_out), .Sel(register_selector_2_reg8),
    .out_4(reg_we_styled_8_out_4));
  assign controlled_buffer_9_out = or_42_out ? MAR_B_q : 5'bz;  // Controlled_Buffer controlled_buffer_11
  Register #(.width(16)) Reg5 (
    .D(controlled_buffer_28_out), .en(reg_we_styled_5_out_4), .clk(and_1_out), .Q(Reg5_q));  // open: clr
  Register #(.width(16)) Reg6 (
    .D(controlled_buffer_28_out), .en(reg_we_styled_6_out_4), .clk(and_1_out), .Q(Reg6_q));  // open: clr
  Register #(.width(16)) Reg7 (
    .D(controlled_buffer_28_out), .en(reg_we_styled_7_out_4), .clk(and_1_out), .Q(Reg7_q));  // open: clr
  Register #(.width(16)) Reg8 (
    .D(controlled_buffer_28_out), .en(reg_we_styled_8_out_4), .clk(and_1_out), .Q(Reg8_q));  // open: clr
  Hex_Digit_Display #(.decimalPoint("false")) hex_digit_display_5 (.value(MBR_A_q_4));
  Hex_Digit_Display #(.decimalPoint("false")) hex_digit_display_6 (.value(MBR_A_q_3));
  Hex_Digit_Display #(.decimalPoint("false")) hex_digit_display_7 (.value(MBR_B_q_4));
  Hex_Digit_Display #(.decimalPoint("false")) hex_digit_display_8 (.value(MBR_B_q_3));
  assign controlled_buffer_12_out = register_selector_2_reg5 ? Reg5_q : 16'bz;  // Controlled_Buffer controlled_buffer_12
  assign controlled_buffer_12_out = register_selector_2_reg6 ? Reg6_q : 16'bz;  // Controlled_Buffer controlled_buffer_13
  Counter #(.max('h1f), .width(5)) MAR_Z (
    .load(or_16_out), .D(controlled_buffer_9_out), .count(and_3_out), .Q(MAR_Z_q), .up(1'b1), .clk(and_1_out));  // open: carry, clr
  Hex_Digit_Display #(.decimalPoint("false")) hex_digit_display_9 (.value(MBR_A_q_2));
  Hex_Digit_Display #(.decimalPoint("false")) hex_digit_display_10 (.value(MBR_A_q));
  Hex_Digit_Display #(.decimalPoint("false")) hex_digit_display_11 (.value(MBR_B_q_2));
  Hex_Digit_Display #(.decimalPoint("false")) hex_digit_display_12 (.value(MBR_B_q));
  assign controlled_buffer_12_out = register_selector_2_reg7 ? Reg7_q : 16'bz;  // Controlled_Buffer controlled_buffer_14
  assign controlled_buffer_12_out = register_selector_2_reg8 ? Reg8_q : 16'bz;  // Controlled_Buffer controlled_buffer_15
  // Probe on controlled_buffer_17_out
  Counter #(.max('h1f), .width(5)) MAR_A (
    .load(or_17_out), .D(ins_split_1_address_a), .count(and_4_out), .Q(MAR_A_q), .up(1'b1), .clk(and_1_out));  // open: carry, clr
  Counter #(.max('h1f), .width(5)) MAR_B (
    .load(or_18_out), .D(controlled_buffer_6_out), .count(and_4_out), .Q(MAR_B_q), .up(1'b1), .clk(and_1_out));  // open: carry, clr
  ALU alu_1 (
    .Flag(Flag_q), .Opcode({Opcode_q[4], Clock_Counter_CC_q[7:4]}), .A(Reg1_q), .B(Reg5_q), .WE(or_35_out),
    .Clock(and_1_out), .Result(alu_1_result), .Overflow(alu_1_overflow));
  assign bit_extender_2_out = {{3{1'b0}}, alu_1_overflow};  // Bit_Extender bit_extender_2
  assign bit_extender_3_out = {{15{1'b0}}, alu_1_overflow};  // Bit_Extender bit_extender_3
  Register #(.width(16)) Terminal (.en(or_41_out), .clk(undriven), .Q(Terminal_q));  // open: D, clr
  Hex_Digit_Display #(.decimalPoint("false")) hex_digit_display_13 (.value(MBR_Z_q[15:12]));
  assign controlled_buffer_16_out = not_5_out ? alu_1_result : 16'bz;  // Controlled_Buffer controlled_buffer_16
  not not_5 (not_5_out, Flag_q);
  assign controlled_buffer_17_out = or_29_out ? controlled_buffer_16_out : 16'bz;  // Controlled_Buffer controlled_buffer_17
  assign controlled_buffer_17_out = or_38_out ? controlled_buffer_27_out : 16'bz;  // Controlled_Buffer controlled_buffer_18
  assign controlled_buffer_3_out = or_38_out ? controlled_buffer_28_out : 16'bz;  // Controlled_Buffer controlled_buffer_19
  assign controlled_buffer_3_out = or_38_out ? controlled_buffer_26_out : 16'bz;  // Controlled_Buffer controlled_buffer_20
  assign controlled_buffer_12_out = or_38_out ? controlled_buffer_27_out : 16'bz;  // Controlled_Buffer controlled_buffer_21
  assign controlled_buffer_12_out = or_38_out ? controlled_buffer_26_out : 16'bz;  // Controlled_Buffer controlled_buffer_22
  Hex_Digit_Display #(.decimalPoint("false")) hex_digit_display_14 (.value(MBR_Z_q[11:8]));
  Hex_Digit_Display #(.decimalPoint("false")) hex_digit_display_15 (.value(MBR_Z_q[7:4]));
  Hex_Digit_Display #(.decimalPoint("false")) hex_digit_display_16 (.value(bit_extender_2_out));
  assign controlled_buffer_16_out = Flag_q ? bit_extender_3_out : 16'bz;  // Controlled_Buffer controlled_buffer_23
  Bus_Select_Styled bus_select_styled_1 (
    .Bus1(or_27_out), .Bus2(or_28_out), .OE(or_30_out), .R_SYS(bus_select_styled_1_r_sys),
    .R_INS(bus_select_styled_1_r_ins), .R_A(bus_select_styled_1_r_a), .R_B(bus_select_styled_1_r_b));
  Hex_Digit_Display #(.decimalPoint("false")) hex_digit_display_17 (.value(MBR_Z_q[3:0]));
  Hex_Digit_Display #(.decimalPoint("false")) hex_digit_display_18 (.value(alu_1_result[15:12]));
  Hex_Digit_Display #(.decimalPoint("false")) hex_digit_display_19 (.value(alu_1_result[11:8]));
  // Probe on controlled_buffer_17_out
  Register #(.width(16)) MBR_Z (
    .D(controlled_buffer_17_out), .en(or_11_out), .clk(and_1_out), .Q(MBR_Z_q));  // open: clr
  Register #(.width(16)) MBR_A (
    .D(controlled_buffer_3_out), .en(or_10_out), .clk(and_1_out),
    .Q({MBR_A_q_4, MBR_A_q_3, MBR_A_q_2, MBR_A_q}));  // open: clr
  Register #(.width(16)) MBR_B (
    .D(controlled_buffer_12_out), .en(or_9_out), .clk(and_1_out),
    .Q({MBR_B_q_4, MBR_B_q_3, MBR_B_q_2, MBR_B_q}));  // open: clr
  assign controlled_buffer_24_out = bus_select_styled_1_r_sys ? Terminal_q : 16'bz;  // Controlled_Buffer controlled_buffer_24
  assign controlled_buffer_24_out = bus_select_styled_1_r_ins ? Terminal_q : 16'bz;  // Controlled_Buffer controlled_buffer_25
  Hex_Digit_Display #(.decimalPoint("false")) hex_digit_display_20 (.value(alu_1_result[7:4]));
  Hex_Digit_Display #(.decimalPoint("false")) hex_digit_display_21 (.value(alu_1_result[3:0]));
  assign controlled_buffer_26_out = or_15_out ? MBR_Z_q : 16'bz;  // Controlled_Buffer controlled_buffer_26
  assign controlled_buffer_27_out = or_14_out ? {MBR_A_q_4, MBR_A_q_3, MBR_A_q_2, MBR_A_q} : 16'bz;  // Controlled_Buffer controlled_buffer_27
  assign controlled_buffer_28_out = or_13_out ? {MBR_B_q_4, MBR_B_q_3, MBR_B_q_2, MBR_B_q} : 16'bz;  // Controlled_Buffer controlled_buffer_28
  assign controlled_buffer_24_out = bus_select_styled_1_r_a ? Terminal_q : 16'bz;  // Controlled_Buffer controlled_buffer_29
  assign controlled_buffer_24_out = bus_select_styled_1_r_b ? Terminal_q : 16'bz;  // Controlled_Buffer controlled_buffer_30
  // Probe on controlled_buffer_3_out
  // Probe on controlled_buffer_12_out
  Counter #(.max('h3), .width(2)) Block_Count (
    .count(or_40_out), .Q(Block_Count_q), .clk(and_1_out));  // open: load, D, carry, up, clr
  MATMULT matmult_1 (
    .A4(Reg4_q), .B1(Reg5_q), .B2(Reg6_q), .B3(Reg7_q), .B4(Reg8_q), .Count(Block_Count_q), .A1(Reg1_q),
    .OE(ins_decoder_1_mat_mult), .A2(Reg2_q), .A3(Reg3_q), .Result(matmult_1_result),
    .Overflow(matmult_1_overflow));
  Register #(.width(16)) register_1 (
    .D(matmult_1_result), .en(and_5_out), .clk(and_1_out), .Q(register_1_q));  // open: clr
  Register #(.width(16)) register_2 (
    .D(matmult_1_result), .en(and_6_out), .clk(and_1_out), .Q(register_2_q));  // open: clr
  Register #(.width(16)) register_3 (
    .D(matmult_1_result), .en(and_7_out), .clk(and_1_out), .Q(register_3_q));  // open: clr
  Register #(.width(16)) register_4 (
    .D(matmult_1_result), .en(and_8_out), .clk(and_1_out), .Q(register_4_q));  // open: clr
  assign controlled_buffer_31_out = not_6_out ? register_1_q : 16'bz;  // Controlled_Buffer controlled_buffer_31
  assign controlled_buffer_32_out = not_6_out ? register_2_q : 16'bz;  // Controlled_Buffer controlled_buffer_32
  not not_6 (not_6_out, Flag_q);
  assign controlled_buffer_33_out = not_6_out ? register_3_q : 16'bz;  // Controlled_Buffer controlled_buffer_33
  assign controlled_buffer_34_out = not_6_out ? register_4_q : 16'bz;  // Controlled_Buffer controlled_buffer_34
  Register #(.width(1)) register_5 (
    .D(matmult_1_overflow), .en(and_5_out), .clk(and_1_out), .Q(register_5_q));  // open: clr
  Register #(.width(1)) register_6 (
    .D(matmult_1_overflow), .en(and_6_out), .clk(and_1_out), .Q(register_6_q));  // open: clr
  Register #(.width(1)) register_7 (
    .D(matmult_1_overflow), .en(and_7_out), .clk(and_1_out), .Q(register_7_q));  // open: clr
  Register #(.width(1)) register_8 (
    .D(matmult_1_overflow), .en(and_8_out), .clk(and_1_out), .Q(register_8_q));  // open: clr
  assign bit_extender_4_out = {{15{1'b0}}, register_5_q};  // Bit_Extender bit_extender_4
  assign bit_extender_5_out = {{15{1'b0}}, register_6_q};  // Bit_Extender bit_extender_5
  assign bit_extender_6_out = {{15{1'b0}}, register_7_q};  // Bit_Extender bit_extender_6
  assign bit_extender_7_out = {{15{1'b0}}, register_8_q};  // Bit_Extender bit_extender_7
  assign controlled_buffer_31_out = Flag_q ? bit_extender_4_out : 16'bz;  // Controlled_Buffer controlled_buffer_35
  assign controlled_buffer_32_out = Flag_q ? bit_extender_5_out : 16'bz;  // Controlled_Buffer controlled_buffer_36
  assign controlled_buffer_33_out = Flag_q ? bit_extender_6_out : 16'bz;  // Controlled_Buffer controlled_buffer_37
  assign controlled_buffer_34_out = Flag_q ? bit_extender_7_out : 16'bz;  // Controlled_Buffer controlled_buffer_38
  RAM_WE_Styled ram_we_styled_1 (
    .Flag(Flag_q), .Ins(ins_decoder_1_move), .Clock(and_1_out), .WE(or_1_out), .A(ram_we_styled_1_a));  // open: B
  RAM #(.addrWidth(5), .dataWidth(16), .trigger("high"), .\type ("nonvolatile")) Instruction_RAM (
    .addr(MAR_Z_q), .we(or_6_out), .oe(or_5_out), .din(controlled_buffer_26_out), .dout(Instruction_RAM_dout));
  RAM #(.addrWidth(5), .dataWidth(16), .trigger("high"), .\type ("nonvolatile")) RAM_A (
    .addr(MAR_A_q), .we(ram_we_styled_1_a), .oe(or_2_out), .din(controlled_buffer_27_out), .dout(RAM_A_dout));
  Selector_2Bit_Styled Block_Selector (
    .Bit0(Block_Count_q[0]), .Bit1(Block_Count_q[1]), .OE(or_39_out), .B00(Block_Selector_b00),
    .B01(Block_Selector_b01), .B10(Block_Selector_b10), .B11(Block_Selector_b11));
  assign controlled_buffer_39_out = Block_Selector_b00 ? controlled_buffer_31_out : 16'bz;  // Controlled_Buffer controlled_buffer_39
  assign controlled_buffer_39_out = Block_Selector_b01 ? controlled_buffer_32_out : 16'bz;  // Controlled_Buffer controlled_buffer_40
  and and_5 (and_5_out, ins_decoder_1_mat_mult, Block_Selector_b00);
  and and_6 (and_6_out, ins_decoder_1_mat_mult, Block_Selector_b01);
  assign controlled_buffer_17_out = ins_decoder_1_block_store ? controlled_buffer_39_out : 16'bz;  // Controlled_Buffer controlled_buffer_41
  assign controlled_buffer_39_out = Block_Selector_b10 ? controlled_buffer_33_out : 16'bz;  // Controlled_Buffer controlled_buffer_42
  assign controlled_buffer_39_out = Block_Selector_b11 ? controlled_buffer_34_out : 16'bz;  // Controlled_Buffer controlled_buffer_43
  and and_7 (and_7_out, ins_decoder_1_mat_mult, Block_Selector_b10);
  and and_8 (and_8_out, ins_decoder_1_mat_mult, Block_Selector_b11);
  assign controlled_buffer_17_out = or_44_out ? Instruction_RAM_dout : 16'bz;  // Controlled_Buffer controlled_buffer_44
  assign controlled_buffer_3_out = or_45_out ? RAM_A_dout : 16'bz;  // Controlled_Buffer controlled_buffer_45
  RAM #(.addrWidth(5), .dataWidth(16), .trigger("high")) System_RAM (
    .addr(MAR_Z_q), .we(ram_we_styled_2_a), .oe(or_7_out), .din(controlled_buffer_26_out),
    .dout(System_RAM_dout));
  RAM_WE_Styled ram_we_styled_2 (.Clock(and_1_out), .WE(or_8_out), .A(ram_we_styled_2_a));  // open: Flag, Ins, B
  RAM_WE_Styled ram_we_styled_3 (
    .Flag(Flag_q), .Ins(ins_decoder_1_move), .Clock(and_1_out), .WE(or_4_out), .B(ram_we_styled_3_b));  // open: A
  RAM #(.addrWidth(5), .dataWidth(16), .trigger("high"), .\type ("nonvolatile")) RAM_B (
    .addr(MAR_B_q), .we(ram_we_styled_3_b), .oe(or_3_out), .din(controlled_buffer_28_out), .dout(RAM_B_dout));
  assign controlled_buffer_17_out = or_43_out ? System_RAM_dout : 16'bz;  // Controlled_Buffer controlled_buffer_46
  assign controlled_buffer_12_out = or_46_out ? RAM_B_dout : 16'bz;  // Controlled_Buffer controlled_buffer_47

  // Notes on the sheet:
  //   contents of Control_Unit_CU (hex, n*v repeats v):
  //   81000000410 18003c800 14*0 300000000306 881002803410 58003c800 13*0 81000000410 40018003c800 14*0
  //   300000000306 881002803410 58003c800 13*0 810008400 c080 81000000410 18003c800 12*0 381000000716
  //   2000003300 18003f809 13*0 881000000710 2000003300 800183fff800 13*0 389000000716 308002803306
  //   308000303306 308001403306 1800ff800 11*0 c800008400 c000004480 c000004480 c000004480 c080
  //   81000000410 18003c800 9*0 c040000000 c040000000 8d040000410 c1c003c800 12*0 300000000306
  //   881002803410 58003c800 13*0 300000000306 881002803410 58003c800 13*0 300000000306 881002803410
  //   58003c800 13*0 300000000306 881002803410 58003c800 13*0 81000000410 18003c800 14*0 20040028000
  //   40000008440 83000004710 18003f809
  //   Opcode
  //   PC
  //   CU
  //   Data in MBR A
  //   Data in MBR B
  //   Data in MBR Z
  //   Overflow
  //   Calculation Result
  //   Flag
endmodule

module HalfAdder (
  input  A,
  input  B,
  output S,
  output C
);

  and and_1 (C, A, B);
  xor xor_1 (S, A, B);

  // Notes on the sheet:
  //   A XOR B
  //   AB
endmodule

module FullAdder (
  input  A,
  input  B,
  input  Cin,
  output Sum,
  output Cout
);

  wire HA0_c, HA0_s, HA1_c;

  HalfAdder HA0 (.A(A), .B(B), .S(HA0_s), .C(HA0_c));
  HalfAdder HA1 (.A(HA0_s), .B(Cin), .S(Sum), .C(HA1_c));
  or or_1 (Cout, HA1_c, HA0_c);

  // Notes on the sheet:
  //   C0 + C1
endmodule

module FullAdder_v1 (
  input  A,
  input  B,
  input  Cin,
  output Sum,
  output Cout
);

  wire C0_out, C1_out, S0_out;

  xor S0 (S0_out, A, B);
  and C0 (C0_out, A, B);
  and C1 (C1_out, S0_out, Cin);
  xor S1 (Sum, S0_out, Cin);
  or C (Cout, C0_out, C1_out);

  // Notes on the sheet:
  //   S0 and S1 are Intermediate Sums
  //   C0 and C1 are Intermediate Carrys
  //   S0
  //   Cin
  //   S0
  //   Cin
  //   C0
  //   C1
  //   S1
endmodule

module ADD_4Bit (
  input  [3:0] A,
  input  [3:0] B,
  input  Cin,
  output [3:0] Sum,
  output Cout
);

  wire fulladder_2_cout, fulladder_3_cout, fulladder_4_cout;

  FullAdder fulladder_1 (.A(A[3]), .B(B[3]), .Cin(fulladder_2_cout), .Sum(Sum[3]), .Cout(Cout));
  FullAdder fulladder_2 (.A(A[2]), .B(B[2]), .Cin(fulladder_3_cout), .Sum(Sum[2]), .Cout(fulladder_2_cout));
  FullAdder fulladder_3 (.A(A[1]), .B(B[1]), .Cin(fulladder_4_cout), .Sum(Sum[1]), .Cout(fulladder_3_cout));
  FullAdder fulladder_4 (.A(A[0]), .B(B[0]), .Cin(Cin), .Sum(Sum[0]), .Cout(fulladder_4_cout));
endmodule

module ADD_8Bit (
  input  [7:0] A,
  input  [7:0] B,
  input  Cin,
  output [7:0] S,
  output Cout
);

  wire add_4bit_2_cout;

  ADD_4Bit add_4bit_1 (.A(A[7:4]), .B(B[7:4]), .Cin(add_4bit_2_cout), .Sum(S[7:4]), .Cout(Cout));
  ADD_4Bit add_4bit_2 (.A(A[3:0]), .B(B[3:0]), .Cin(Cin), .Sum(S[3:0]), .Cout(add_4bit_2_cout));
  // Probe on S
endmodule

module ADD_16Bit (
  input  [15:0] A,
  input  [15:0] B,
  input  Cin,
  output [15:0] Sum,
  output Cout
);

  wire A0_cout, A4_cout, A8_cout;

  ADD_4Bit A12 (.A(A[15:12]), .B(B[15:12]), .Cin(A8_cout), .Sum(Sum[15:12]), .Cout(Cout));
  ADD_4Bit A8 (.A(A[11:8]), .B(B[11:8]), .Cin(A4_cout), .Sum(Sum[11:8]), .Cout(A8_cout));
  ADD_4Bit A4 (.A(A[7:4]), .B(B[7:4]), .Cin(A0_cout), .Sum(Sum[7:4]), .Cout(A4_cout));
  ADD_4Bit A0 (.A(A[3:0]), .B(B[3:0]), .Cin(Cin), .Sum(Sum[3:0]), .Cout(A0_cout));
endmodule

module ADD_16Bit_Final (
  input  [15:0] A,
  input  [15:0] B,
  output [15:0] Sum,
  output Cout
);

  ADD_16Bit add_16bit_1 (.A(A), .B(B), .Sum(Sum), .Cout(Cout));  // open: Cin
endmodule

module ADD_SUB_2Bit (
  input  A,
  input  B,
  input  Carry_in,
  input  Sub,
  output Sum,
  output Carry_out
);

  wire or_1_out, xor_1_out;

  xor xor_1 (xor_1_out, B, Sub);
  or or_1 (or_1_out, Carry_in, Sub);
  FullAdder fulladder_1 (.A(A), .B(xor_1_out), .Cin(or_1_out), .Sum(Sum), .Cout(Carry_out));
endmodule

module ADD_SUB_4Bit (
  input  [3:0] A,
  input  [3:0] B,
  input  Carry_in,
  input  Sub,
  output [3:0] Sum,
  output Carry_out
);

  wire or_1_out;
  wire [3:0] bit_extender_1_out, xor_1_out;

  assign bit_extender_1_out = {{3{Sub}}, Sub};  // Bit_Extender bit_extender_1
  // Probe on bit_extender_1_out
  assign xor_1_out = B ^ bit_extender_1_out;  // XOR_Gate xor_1, 4 bits wide
  or or_1 (or_1_out, Carry_in, Sub);
  ADD_4Bit add_4bit_1 (.A(A), .B(xor_1_out), .Cin(or_1_out), .Sum(Sum), .Cout(Carry_out));
endmodule

module ADD_SUB_16Bit (
  input  [15:0] A,
  input  [15:0] B,
  input  Cin,
  input  Sub,
  output [15:0] Sum,
  output Cout
);

  wire or_1_out;
  wire [15:0] bit_extender_1_out, xor_1_out;

  assign bit_extender_1_out = {{15{Sub}}, Sub};  // Bit_Extender bit_extender_1
  assign xor_1_out = B ^ bit_extender_1_out;  // XOR_Gate xor_1, 16 bits wide
  or or_1 (or_1_out, Cin, Sub);
  ADD_16Bit add_16bit_1 (.A(A), .B(xor_1_out), .Cin(or_1_out), .Sum(Sum), .Cout(Cout));
endmodule

module ADD_SUB_16Bit_DualSub (
  input  [15:0] A,
  input  [15:0] B,
  input  Cin,
  input  Sub,
  output [15:0] Sum,
  output Cout
);

  wire add_sub_16bit_1_cout, and_1_out, not_1_out, not_2_out;
  wire [15:0] add_sub_16bit_1_sum;

  // Probe on add_sub_16bit_1_sum
  ADD_SUB_16Bit add_sub_16bit_1 (
    .A(A), .B(B), .Cin(Cin), .Sub(Sub), .Sum(add_sub_16bit_1_sum), .Cout(add_sub_16bit_1_cout));
  not not_1 (not_1_out, add_sub_16bit_1_cout);
  and and_1 (and_1_out, not_1_out, Sub);
  not not_2 (not_2_out, Sub);
  and and_2 (Cout, not_2_out, add_sub_16bit_1_cout);
  ADD_SUB_16Bit add_sub_16bit_2 (
    .A({16{1'b0}}), .B(add_sub_16bit_1_sum), .Cin(and_1_out), .Sub(and_1_out), .Sum(Sum));  // open: Cout

  // Notes on the sheet:
  //   ADD SUB (handles A<B case)
  //   S1
  //   If A<B and Sub=1, then S2 = 2s complement of S1. If not, then S2 = S1.
  //   If Sub=1, then Cout must be 0 as there is no overflow in subtraction.
  //   Sub'
  //   C1
endmodule

module CMP_Base (
  input  A,
  input  B,
  output LT,
  output EQ,
  output GT
);

  wire not_1_out, not_2_out;

  not not_1 (not_1_out, A);
  and and_1 (LT, not_1_out, B);
  and and_2 (GT, A, not_2_out);
  not not_2 (not_2_out, B);
  xnor xnor_1 (EQ, A, B);

  // Notes on the sheet:
  //   A
  //   B
  //   A' AND B
  //   A XNOR B
  //   A AND B'
endmodule

module CMP_1Bit (
  input  A,
  input  B,
  input  LT_in,
  input  EQ_in,
  input  GT_in,
  output LT,
  output EQ,
  output GT
);

  wire and_1_out, and_2_out, cmp_base_1_eq, cmp_base_1_gt, cmp_base_1_lt;

  CMP_Base cmp_base_1 (.A(A), .B(B), .LT(cmp_base_1_lt), .EQ(cmp_base_1_eq), .GT(cmp_base_1_gt));
  and and_1 (and_1_out, LT_in, cmp_base_1_eq);
  and and_2 (and_2_out, cmp_base_1_eq, GT_in);
  or or_1 (LT, and_1_out, cmp_base_1_lt);
  and and_3 (EQ, cmp_base_1_eq, EQ_in);
  or or_2 (GT, cmp_base_1_gt, and_2_out);

  // Notes on the sheet:
  //   Comparator (1 Bit, Extendable)
endmodule

module CMP_2Bit (
  input  [1:0] A,
  input  [1:0] B,
  input  LT_in,
  input  EQ_in,
  input  GT_in,
  output LT,
  output EQ,
  output GT
);

  wire cmp_1bit_1_eq, cmp_1bit_1_gt, cmp_1bit_1_lt;

  CMP_1Bit cmp_1bit_1 (
    .A(A[0]), .B(B[0]), .LT_in(LT_in), .EQ_in(EQ_in), .GT_in(GT_in), .LT(cmp_1bit_1_lt), .EQ(cmp_1bit_1_eq),
    .GT(cmp_1bit_1_gt));
  CMP_1Bit cmp_1bit_2 (
    .A(A[1]), .B(B[1]), .LT_in(cmp_1bit_1_lt), .EQ_in(cmp_1bit_1_eq), .GT_in(cmp_1bit_1_gt), .LT(LT),
    .EQ(EQ), .GT(GT));
endmodule

module CMP_4Bit (
  input  [3:0] A,
  input  [3:0] B,
  input  LT_in,
  input  EQ_in,
  input  GT_in,
  output LT,
  output EQ,
  output GT
);

  wire cmp_2bit_1_eq, cmp_2bit_1_gt, cmp_2bit_1_lt;

  CMP_2Bit cmp_2bit_1 (
    .A(A[1:0]), .B(B[1:0]), .LT_in(LT_in), .EQ_in(EQ_in), .GT_in(GT_in), .LT(cmp_2bit_1_lt),
    .EQ(cmp_2bit_1_eq), .GT(cmp_2bit_1_gt));
  CMP_2Bit cmp_2bit_2 (
    .A(A[3:2]), .B(B[3:2]), .LT_in(cmp_2bit_1_lt), .EQ_in(cmp_2bit_1_eq), .GT_in(cmp_2bit_1_gt), .LT(LT),
    .EQ(EQ), .GT(GT));
endmodule

module CMP_4Bit_Styled (
  input  [3:0] A,
  input  [3:0] B,
  output LT,
  output EQ,
  output GT
);

  CMP_4Bit cmp_4bit_1 (.A(A), .B(B), .EQ_in(1'b1), .LT(LT), .EQ(EQ), .GT(GT));  // open: LT_in, GT_in
endmodule

module CMP_8Bit (
  input  [7:0] A,
  input  [7:0] B,
  input  LT_in,
  input  EQ_in,
  input  GT_in,
  output LT,
  output EQ,
  output GT
);

  wire cmp_4bit_1_eq, cmp_4bit_1_gt, cmp_4bit_1_lt;

  CMP_4Bit cmp_4bit_1 (
    .A(A[3:0]), .B(B[3:0]), .LT_in(LT_in), .EQ_in(EQ_in), .GT_in(GT_in), .LT(cmp_4bit_1_lt),
    .EQ(cmp_4bit_1_eq), .GT(cmp_4bit_1_gt));
  CMP_4Bit cmp_4bit_2 (
    .A(A[7:4]), .B(B[7:4]), .LT_in(cmp_4bit_1_lt), .EQ_in(cmp_4bit_1_eq), .GT_in(cmp_4bit_1_gt), .LT(LT),
    .EQ(EQ), .GT(GT));
endmodule

module CMP_16Bit (
  input  [15:0] A,
  input  [15:0] B,
  input  LT_in,
  input  EQ_in,
  input  GT_in,
  output LT,
  output EQ,
  output GT
);

  wire cmp_8bit_1_eq, cmp_8bit_1_gt, cmp_8bit_1_lt;

  CMP_8Bit cmp_8bit_1 (
    .A(A[7:0]), .B(B[7:0]), .LT_in(LT_in), .EQ_in(EQ_in), .GT_in(GT_in), .LT(cmp_8bit_1_lt),
    .EQ(cmp_8bit_1_eq), .GT(cmp_8bit_1_gt));
  CMP_8Bit cmp_8bit_2 (
    .A(A[15:8]), .B(B[15:8]), .LT_in(cmp_8bit_1_lt), .EQ_in(cmp_8bit_1_eq), .GT_in(cmp_8bit_1_gt), .LT(LT),
    .EQ(EQ), .GT(GT));
endmodule

module CMP_16Bit_Final (
  input  [15:0] A,
  input  [15:0] B,
  output LT,
  output EQ,
  output GT
);

  CMP_16Bit cmp_16bit_1 (.A(A), .B(B), .LT_in(1'b0), .EQ_in(1'b1), .GT_in(1'b0), .LT(LT), .EQ(EQ), .GT(GT));

  // Notes on the sheet:
  //   Final 16-Bit Comparator
endmodule

module MUX_2Bit (
  input  [1:0] A,
  input  S,
  output X
);

  wire and_1_out, and_2_out, not_1_out;

  and and_1 (and_1_out, A[0], not_1_out);
  not not_1 (not_1_out, S);
  and and_2 (and_2_out, A[1], S);
  or or_1 (X, and_1_out, and_2_out);

  // Notes on the sheet:
  //   2-1 Multiplexer
  //   When S = 0, X = A0
  //   When S = 1, X = A1
  //   S'A + SB
endmodule

module MUX_4Bit (
  input  [3:0] A,
  input  [1:0] S,
  output X
);

  wire [1:0] mux_2bit_1_x;

  MUX_2Bit mux_2bit_1 (.A(A[1:0]), .S(S[0]), .X(mux_2bit_1_x[0]));
  MUX_2Bit mux_2bit_2 (.A(A[3:2]), .S(S[0]), .X(mux_2bit_1_x[1]));
  MUX_2Bit mux_2bit_3 (.A(mux_2bit_1_x), .S(S[1]), .X(X));

  // Notes on the sheet:
  //   MUX([A0, A1], [S0])
endmodule

module MUX_8Bit (
  input  [7:0] A,
  input  [2:0] S,
  output X
);

  wire [1:0] M0_x;

  MUX_4Bit M0 (.A(A[3:0]), .S(S[1:0]), .X(M0_x[0]));
  MUX_4Bit M1 (.A(A[7:4]), .S(S[1:0]), .X(M0_x[1]));
  MUX_2Bit mux_2bit_1 (.A(M0_x), .S(S[2]), .X(X));
endmodule

module MUX_16Bit (
  input  [15:0] A,
  input  [3:0] S,
  output X
);

  wire [3:0] M0_x;

  MUX_4Bit M0 (.A(A[3:0]), .S(S[1:0]), .X(M0_x[0]));
  MUX_4Bit M1 (.A(A[7:4]), .S(S[1:0]), .X(M0_x[1]));
  MUX_4Bit M2 (.A(A[11:8]), .S(S[1:0]), .X(M0_x[2]));
  MUX_4Bit M3 (.A(A[15:12]), .S(S[1:0]), .X(M0_x[3]));
  MUX_4Bit mux_4bit_1 (.A(M0_x), .S(S[3:2]), .X(X));

  // Notes on the sheet:
  //   MUX([A0, A1, A2, A3], [S0, S1])
endmodule

module MULT_1x1 (
  input  A,
  input  B,
  output [1:0] AB
);

  wire and_1_out;

  and and_1 (and_1_out, A, B);
  assign AB = {{1{1'b0}}, and_1_out};  // Bit_Extender bit_extender_1
endmodule

module MULT_2x2 (
  input  [1:0] A,
  input  [1:0] B,
  output [3:0] P
);

  wire [1:0] mult_1x1_1_ab, mult_1x1_2_ab, mult_1x1_3_ab, mult_1x1_4_ab, undriven, undriven_4;
  wire [3:0] add_4bit_1_sum, add_4bit_2_sum, undriven_2, undriven_3;

  // Probe on A
  // Probe on B
  MULT_1x1 mult_1x1_1 (.A(A[0]), .B(B[0]), .AB(mult_1x1_1_ab));
  MULT_1x1 mult_1x1_2 (.A(A[0]), .B(B[1]), .AB(mult_1x1_2_ab));
  MULT_1x1 mult_1x1_3 (.A(A[1]), .B(B[0]), .AB(mult_1x1_3_ab));
  MULT_1x1 mult_1x1_4 (.A(A[1]), .B(B[1]), .AB(mult_1x1_4_ab));
  ADD_4Bit add_4bit_1 (
    .A({undriven, mult_1x1_1_ab}), .B({undriven_2[3], mult_1x1_2_ab, undriven_2[0]}), .Sum(add_4bit_1_sum));  // open: Cin, Cout
  ADD_4Bit add_4bit_2 (
    .A({undriven_3[3], mult_1x1_3_ab, undriven_3[0]}), .B({mult_1x1_4_ab, undriven_4}), .Sum(add_4bit_2_sum));  // open: Cin, Cout
  // Probe on P
  ADD_4Bit add_4bit_3 (.A(add_4bit_1_sum), .B(add_4bit_2_sum), .Sum(P));  // open: Cin, Cout
endmodule

module MULT_4x4 (
  input  [3:0] A,
  input  [3:0] B,
  output [7:0] P
);

  wire [3:0] mult_2x2_1_p, mult_2x2_2_p, mult_2x2_3_p, mult_2x2_4_p, undriven, undriven_4;
  wire [7:0] add_8bit_1_s, add_8bit_2_s, undriven_2, undriven_3;

  // Probe on A
  // Probe on B
  MULT_2x2 mult_2x2_1 (.A(A[1:0]), .B(B[1:0]), .P(mult_2x2_1_p));
  MULT_2x2 mult_2x2_2 (.A(A[1:0]), .B(B[3:2]), .P(mult_2x2_2_p));
  MULT_2x2 mult_2x2_3 (.A(A[3:2]), .B(B[1:0]), .P(mult_2x2_3_p));
  MULT_2x2 mult_2x2_4 (.A(A[3:2]), .B(B[3:2]), .P(mult_2x2_4_p));
  ADD_8Bit add_8bit_1 (
    .A({undriven, mult_2x2_1_p}), .B({undriven_2[7:6], mult_2x2_2_p, undriven_2[1:0]}), .S(add_8bit_1_s));  // open: Cin, Cout
  ADD_8Bit add_8bit_2 (
    .A({undriven_3[7:6], mult_2x2_3_p, undriven_3[1:0]}), .B({mult_2x2_4_p, undriven_4}), .S(add_8bit_2_s));  // open: Cin, Cout
  // Probe on P
  ADD_8Bit add_8bit_3 (.A(add_8bit_1_s), .B(add_8bit_2_s), .S(P));  // open: Cin, Cout
endmodule

module MULT_8x8 (
  input  [7:0] A,
  input  [7:0] B,
  output [15:0] P
);

  wire [7:0] mult_4x4_1_p, mult_4x4_2_p, mult_4x4_3_p, mult_4x4_4_p, undriven, undriven_4;
  wire [15:0] add_16bit_1_sum, add_16bit_2_sum, undriven_2, undriven_3;

  MULT_4x4 mult_4x4_1 (.A(A[3:0]), .B(B[3:0]), .P(mult_4x4_1_p));
  MULT_4x4 mult_4x4_2 (.A(A[3:0]), .B(B[7:4]), .P(mult_4x4_2_p));
  MULT_4x4 mult_4x4_3 (.A(A[7:4]), .B(B[3:0]), .P(mult_4x4_3_p));
  MULT_4x4 mult_4x4_4 (.A(A[7:4]), .B(B[7:4]), .P(mult_4x4_4_p));
  ADD_16Bit add_16bit_1 (
    .A({undriven, mult_4x4_1_p}), .B({undriven_2[15:12], mult_4x4_2_p, undriven_2[3:0]}),
    .Sum(add_16bit_1_sum));  // open: Cin, Cout
  ADD_16Bit add_16bit_2 (
    .A({undriven_3[15:12], mult_4x4_3_p, undriven_3[3:0]}), .B({mult_4x4_4_p, undriven_4}),
    .Sum(add_16bit_2_sum));  // open: Cin, Cout
  ADD_16Bit add_16bit_3 (.A(add_16bit_1_sum), .B(add_16bit_2_sum), .Sum(P));  // open: Cin, Cout
endmodule

module INS_SPLIT (
  input  [15:0] Instruction,
  output Flag,
  output [4:0] Opcode,
  output [4:0] Address_A,
  output [4:0] Address_B
);


  assign Address_A = Instruction[9:5];
  assign Address_B = Instruction[4:0];
  assign Flag = Instruction[15];
  assign Opcode = Instruction[14:10];
endmodule

module ALU (
  input  Flag,
  input  [4:0] Opcode,
  input  [15:0] A,
  input  [15:0] B,
  input  WE,
  input  Clock,
  output [15:0] Result,
  output Overflow
);

  wire AddSub_carry, controlled_buffer_7_out, opcode_decoder_5bit_1_add_sub, opcode_decoder_5bit_1_compare,
       opcode_decoder_5bit_1_logical_and, opcode_decoder_5bit_1_logical_not,
       opcode_decoder_5bit_1_logical_xor, opcode_decoder_5bit_1_mult;
  wire [15:0] AddSub_sum, and_1_out, CMP_c, controlled_buffer_1_out, MULT_product, not_1_out, xor_1_out;

  Opcode_Decoder_5Bit opcode_decoder_5bit_1 (
    .in_1(Opcode), .Add_Sub(opcode_decoder_5bit_1_add_sub), .Mult(opcode_decoder_5bit_1_mult),
    .Compare(opcode_decoder_5bit_1_compare), .Logical_AND(opcode_decoder_5bit_1_logical_and),
    .Logical_XOR(opcode_decoder_5bit_1_logical_xor), .Logical_NOT(opcode_decoder_5bit_1_logical_not));  // open: Reserved, out_4, Store, Mem_Swap, Reg_Swap, Block_Load, Block_Store, MATMULT, NOP_Halt, MOVE
  ADD_ALU AddSub (.A(A), .B(B), .Sub(Flag), .Sum(AddSub_sum), .Carry(AddSub_carry));  // open: Cin
  MULT_ALU MULT (.A(A), .B(B), .Product(MULT_product));
  CMP_ALU CMP (.A(A), .B(B), .C(CMP_c));
  assign and_1_out = A & B;  // AND_Gate and_1, 16 bits wide
  assign xor_1_out = A ^ B;  // XOR_Gate xor_1, 16 bits wide
  assign not_1_out = ~A;  // NOT_Gate not_1, 16 bits wide
  assign controlled_buffer_1_out = opcode_decoder_5bit_1_add_sub ? AddSub_sum : 16'bz;  // Controlled_Buffer controlled_buffer_1
  assign controlled_buffer_1_out = opcode_decoder_5bit_1_mult ? MULT_product : 16'bz;  // Controlled_Buffer controlled_buffer_2
  assign controlled_buffer_1_out = opcode_decoder_5bit_1_compare ? CMP_c : 16'bz;  // Controlled_Buffer controlled_buffer_3
  assign controlled_buffer_1_out = opcode_decoder_5bit_1_logical_and ? and_1_out : 16'bz;  // Controlled_Buffer controlled_buffer_4
  assign controlled_buffer_1_out = opcode_decoder_5bit_1_logical_xor ? xor_1_out : 16'bz;  // Controlled_Buffer controlled_buffer_5
  assign controlled_buffer_1_out = opcode_decoder_5bit_1_logical_not ? not_1_out : 16'bz;  // Controlled_Buffer controlled_buffer_6
  assign controlled_buffer_7_out = opcode_decoder_5bit_1_add_sub ? AddSub_carry : 1'bz;  // Controlled_Buffer controlled_buffer_7
  Register #(.width(16)) register_1 (.D(controlled_buffer_1_out), .en(WE), .clk(Clock), .Q(Result));  // open: clr
  Register #(.width(1)) register_2 (.D(controlled_buffer_7_out), .en(WE), .clk(Clock), .Q(Overflow));  // open: clr
endmodule

module ADD_ALU (
  input  [15:0] A,
  input  [15:0] B,
  input  Cin,
  input  Sub,
  output [15:0] Sum,
  output Carry
);

  ADD_SUB_16Bit add_sub_16bit_1 (.A(A), .B(B), .Cin(Cin), .Sub(Sub), .Sum(Sum), .Cout(Carry));
endmodule

module MISC_ALU (
  input  [15:0] A,
  input  [15:0] B,
  output [15:0] X
);
endmodule

module MULT_ALU (
  input  [15:0] A,
  input  [15:0] B,
  output [15:0] Product
);

  wire [7:0] bit_extender_1_out, bit_extender_2_out;

  Bit_Extender #(.in_width(16), .out_width(8), .\type ("zero")) bit_extender_1 (.in(A), .out(bit_extender_1_out));
  Bit_Extender #(.in_width(16), .out_width(8), .\type ("zero")) bit_extender_2 (.in(B), .out(bit_extender_2_out));
  MULT_8x8 mult_8x8_1 (.A(bit_extender_1_out), .B(bit_extender_2_out), .P(Product));
endmodule

module CMP_ALU (
  input  [15:0] A,
  input  [15:0] B,
  output [15:0] C
);

  wire [2:0] cmp_16bit_final_1_lt;

  CMP_16Bit_Final cmp_16bit_final_1 (
    .A(A), .B(B), .LT(cmp_16bit_final_1_lt[0]), .EQ(cmp_16bit_final_1_lt[1]), .GT(cmp_16bit_final_1_lt[2]));
  assign C = {{13{1'b0}}, cmp_16bit_final_1_lt};  // Bit_Extender bit_extender_1
endmodule

module Decoder_1Bit (
  input  A,
  input  OE,
  output [1:0] B
);

  wire [0:0] not_1_out;
  wire [1:0] bit_extender_1_out;

  not not_1 (not_1_out[0], A);
  assign bit_extender_1_out = {{1{OE}}, OE};  // Bit_Extender bit_extender_1
  assign B = {A, not_1_out[0]} & bit_extender_1_out;  // AND_Gate and_1, 2 bits wide
endmodule

module Decoder_2Bit (
  input  [1:0] A,
  input  OE,
  output [3:0] B
);

  wire not_1_out;
  wire [1:0] decoder_1bit_1_b, decoder_1bit_2_b;
  wire [3:0] bit_extender_1_out;

  not not_1 (not_1_out, A[1]);
  Decoder_1Bit decoder_1bit_1 (.A(A[0]), .OE(not_1_out), .B(decoder_1bit_1_b));
  Decoder_1Bit decoder_1bit_2 (.A(A[0]), .OE(A[1]), .B(decoder_1bit_2_b));
  assign B = {decoder_1bit_2_b, decoder_1bit_1_b} & bit_extender_1_out;  // AND_Gate and_1, 4 bits wide
  assign bit_extender_1_out = {{3{OE}}, OE};  // Bit_Extender bit_extender_1
endmodule

module Decoder_3Bit (
  input  [2:0] A,
  input  OE,
  output [7:0] B
);

  wire not_1_out;
  wire [3:0] decoder_2bit_1_b, decoder_2bit_2_b;
  wire [7:0] bit_extender_1_out;

  not not_1 (not_1_out, A[2]);
  Decoder_2Bit decoder_2bit_1 (.A(A[1:0]), .OE(not_1_out), .B(decoder_2bit_1_b));
  Decoder_2Bit decoder_2bit_2 (.A(A[1:0]), .OE(A[2]), .B(decoder_2bit_2_b));
  assign B = {decoder_2bit_2_b, decoder_2bit_1_b} & bit_extender_1_out;  // AND_Gate and_1, 8 bits wide
  assign bit_extender_1_out = {{7{OE}}, OE};  // Bit_Extender bit_extender_1
endmodule

module Decoder_4Bit (
  input  [3:0] A,
  input  OE,
  output [15:0] B
);

  wire not_1_out;
  wire [7:0] decoder_3bit_1_b, decoder_3bit_2_b;
  wire [15:0] bit_extender_1_out;

  not not_1 (not_1_out, A[3]);
  Decoder_3Bit decoder_3bit_1 (.A(A[2:0]), .OE(not_1_out), .B(decoder_3bit_1_b));
  Decoder_3Bit decoder_3bit_2 (.A(A[2:0]), .OE(A[3]), .B(decoder_3bit_2_b));
  assign B = {decoder_3bit_2_b, decoder_3bit_1_b} & bit_extender_1_out;  // AND_Gate and_1, 16 bits wide
  assign bit_extender_1_out = {{15{OE}}, OE};  // Bit_Extender bit_extender_1
endmodule

module Decoder_5Bit (
  input  [4:0] A,
  input  OE,
  output [31:0] B
);

  wire not_1_out;
  wire [15:0] decoder_4bit_1_b, decoder_4bit_2_b;
  wire [31:0] bit_extender_1_out;

  not not_1 (not_1_out, A[4]);
  Decoder_4Bit decoder_4bit_1 (.A(A[3:0]), .OE(not_1_out), .B(decoder_4bit_1_b));
  Decoder_4Bit decoder_4bit_2 (.A(A[3:0]), .OE(A[4]), .B(decoder_4bit_2_b));
  assign B = {decoder_4bit_2_b, decoder_4bit_1_b} & bit_extender_1_out;  // AND_Gate and_1, 32 bits wide
  assign bit_extender_1_out = {{31{OE}}, OE};  // Bit_Extender bit_extender_1
endmodule

module Decoder_5Bit_Split (
  input  [4:0] A,
  input  OE,
  output B00000,
  output B00001,
  output B00010,
  output B00011,
  output B00100,
  output B00101,
  output B00110,
  output B00111,
  output B01000,
  output B01001,
  output B01010,
  output B01011,
  output B01100,
  output B01101,
  output B01110,
  output B01111,
  output B10000,
  output B10001,
  output B10010,
  output B10011,
  output B10100,
  output B10101,
  output B10110,
  output B10111,
  output B11000,
  output B11001,
  output B11010,
  output B11011,
  output B11100,
  output B11101,
  output B11110,
  output B11111
);

  Decoder_5Bit decoder_5bit_1 (
    .A(A), .OE(OE),
    .B({B11111, B11110, B11101, B11100, B11011, B11010, B11001, B11000, B10111, B10110, B10101, B10100, B10011, B10010, B10001, B10000, B01111, B01110, B01101, B01100, B01011, B01010, B01001, B01000, B00111, B00110, B00101, B00100, B00011, B00010, B00001, B00000}));
endmodule

module Opcode_Decoder_5Bit (
  input  [4:0] in_1,
  output Reserved,
  output Add_Sub,
  output out_4,
  output Mult,
  output Store,
  output Mem_Swap,
  output Reg_Swap,
  output Block_Load,
  output Block_Store,
  output MATMULT,
  output Compare,
  output Logical_AND,
  output Logical_XOR,
  output Logical_NOT,
  output NOP_Halt,
  output MOVE
);

  Decoder_5Bit_Split decoder_5bit_split_1 (
    .A(in_1), .OE(1'b1), .B00000(Reserved), .B00001(Add_Sub), .B00010(out_4), .B00011(Mult), .B00100(Store),
    .B00101(Mem_Swap), .B00110(Reg_Swap), .B00111(Block_Load), .B01000(Block_Store), .B01001(MATMULT),
    .B01010(Compare), .B01011(Logical_AND), .B01100(Logical_XOR), .B01101(Logical_NOT), .B01110(NOP_Halt),
    .B01111(MOVE));  // open: B10000, B10001, B10010, B10011, B10100, B10101, B10110, B10111, B11000, B11001, B11010, B11011, B11100, B11101, B11110, B11111
endmodule

module Bus_Select_Styled (
  input  Bus1,
  input  Bus2,
  input  OE,
  output R_SYS,
  output R_INS,
  output R_A,
  output R_B
);

  Decoder_2Bit decoder_2bit_1 (.A({Bus2, Bus1}), .OE(OE), .B({R_B, R_A, R_INS, R_SYS}));
endmodule

module Selector_1Bit_Styled (
  input  S,
  output S0,
  output S1
);

  Decoder_1Bit decoder_1bit_1 (.A(S), .OE(1'b1), .B({S1, S0}));
endmodule

module ADD_5Bit_Styled (
  input  [4:0] A,
  input  [4:0] B,
  output [4:0] Sum
);

  wire fulladder_1_cout, fulladder_2_cout, fulladder_3_cout, fulladder_4_cout, fulladder_5_cout, undriven;

  FullAdder fulladder_1 (.A(A[4]), .B(B[4]), .Cin(fulladder_2_cout), .Sum(Sum[4]), .Cout(fulladder_1_cout));
  FullAdder fulladder_2 (.A(A[3]), .B(B[3]), .Cin(fulladder_3_cout), .Sum(Sum[3]), .Cout(fulladder_2_cout));
  FullAdder fulladder_3 (.A(A[2]), .B(B[2]), .Cin(fulladder_4_cout), .Sum(Sum[2]), .Cout(fulladder_3_cout));
  FullAdder fulladder_4 (.A(A[1]), .B(B[1]), .Cin(fulladder_5_cout), .Sum(Sum[1]), .Cout(fulladder_4_cout));
  FullAdder fulladder_5 (.A(A[0]), .B(B[0]), .Cin(undriven), .Sum(Sum[0]), .Cout(fulladder_5_cout));
endmodule

module Selector_2Bit_Styled (
  input  Bit0,
  input  Bit1,
  input  OE,
  output B00,
  output B01,
  output B10,
  output B11
);

  Decoder_2Bit decoder_2bit_1 (.A({Bit1, Bit0}), .OE(OE), .B({B11, B10, B01, B00}));
endmodule

module MATMULT (
  input  [15:0] A1,
  input  [15:0] A2,
  input  [15:0] A3,
  input  [15:0] A4,
  input  [15:0] B1,
  input  [15:0] B2,
  input  [15:0] B3,
  input  [15:0] B4,
  input  [1:0] Count,
  input  OE,
  output [15:0] Result,
  output Overflow
);

  wire add_alu_1_carry, not_1_out, not_2_out, not_3_out, not_4_out;
  wire [15:0] add_alu_1_sum, controlled_buffer_1_out, controlled_buffer_2_out, controlled_buffer_3_out,
       controlled_buffer_4_out, mult_alu_1_product, mult_alu_2_product;

  assign controlled_buffer_1_out = Count[0] ? B2 : 16'bz;  // Controlled_Buffer controlled_buffer_1
  assign controlled_buffer_2_out = Count[0] ? B4 : 16'bz;  // Controlled_Buffer controlled_buffer_2
  assign controlled_buffer_3_out = Count[1] ? A3 : 16'bz;  // Controlled_Buffer controlled_buffer_3
  assign controlled_buffer_4_out = Count[1] ? A4 : 16'bz;  // Controlled_Buffer controlled_buffer_4
  assign controlled_buffer_2_out = not_1_out ? B3 : 16'bz;  // Controlled_Buffer controlled_buffer_5
  not not_1 (not_1_out, Count[0]);
  not not_2 (not_2_out, Count[1]);
  assign controlled_buffer_3_out = not_3_out ? A1 : 16'bz;  // Controlled_Buffer controlled_buffer_6
  not not_3 (not_3_out, Count[1]);
  assign controlled_buffer_1_out = not_4_out ? B1 : 16'bz;  // Controlled_Buffer controlled_buffer_7
  not not_4 (not_4_out, Count[0]);
  assign controlled_buffer_4_out = not_2_out ? A2 : 16'bz;  // Controlled_Buffer controlled_buffer_8
  MULT_ALU mult_alu_1 (.A(controlled_buffer_3_out), .B(controlled_buffer_1_out), .Product(mult_alu_1_product));
  MULT_ALU mult_alu_2 (.A(controlled_buffer_4_out), .B(controlled_buffer_2_out), .Product(mult_alu_2_product));
  ADD_ALU add_alu_1 (
    .A(mult_alu_1_product), .B(mult_alu_2_product), .Sum(add_alu_1_sum), .Carry(add_alu_1_carry));  // open: Cin, Sub
  assign Result = OE ? add_alu_1_sum : 16'bz;  // Controlled_Buffer controlled_buffer_9
  and and_1 (Overflow, add_alu_1_carry, OE);
endmodule

module INS_Decoder (
  input  Flag,
  input  [4:0] Opcode,
  output Reg_Swap,
  output Block_Load,
  output Block_Store,
  output Mat_Mult,
  output Move,
  output Halt
);

  wire decoder_5bit_split_1_b00001, decoder_5bit_split_1_b00011, decoder_5bit_split_1_b01010,
       decoder_5bit_split_1_b01011, decoder_5bit_split_1_b01100, decoder_5bit_split_1_b01101,
       decoder_5bit_split_1_b01110, or_1_out;

  Decoder_5Bit_Split decoder_5bit_split_1 (
    .A(Opcode), .OE(1'b1), .B00001(decoder_5bit_split_1_b00001), .B00011(decoder_5bit_split_1_b00011),
    .B00110(Reg_Swap), .B00111(Block_Load), .B01000(Block_Store), .B01001(Mat_Mult),
    .B01010(decoder_5bit_split_1_b01010), .B01011(decoder_5bit_split_1_b01011),
    .B01100(decoder_5bit_split_1_b01100), .B01101(decoder_5bit_split_1_b01101),
    .B01110(decoder_5bit_split_1_b01110), .B01111(Move));  // open: B00000, B00010, B00100, B00101, B10000, B10001, B10010, B10011, B10100, B10101, B10110, B10111, B11000, B11001, B11010, B11011, B11100, B11101, B11110, B11111
  // Probe on or_1_out
  or or_1 (or_1_out, decoder_5bit_split_1_b00001, decoder_5bit_split_1_b00011, decoder_5bit_split_1_b01010, decoder_5bit_split_1_b01011, decoder_5bit_split_1_b01100, decoder_5bit_split_1_b01101);
  and and_1 (Halt, Flag, decoder_5bit_split_1_b01110);
endmodule

module Delayer (
  input  [4:0] Delay,
  input  Clock,
  output Clock_Out
);

  wire and_1_out, cmp_5bit_styled_1_eq, not_1_out;
  wire [4:0] counter_1_q;

  Counter #(.max('h1f), .width(5)) counter_1 (
    .load(cmp_5bit_styled_1_eq), .D({5{1'b0}}), .count(1'b1), .Q(counter_1_q), .up(1'b1), .clk(Clock));  // open: carry, clr
  CMP_5Bit_Styled cmp_5bit_styled_1 (.A(Delay), .B(counter_1_q), .EQ(cmp_5bit_styled_1_eq));  // open: LT, GT
  Register #(.width(1)) register_1 (.D(cmp_5bit_styled_1_eq), .en(Clock), .clk(Clock), .Q(Clock_Out), .clr(and_1_out));
  not not_1 (not_1_out, Clock);
  and and_1 (and_1_out, not_1_out, Clock_Out);
endmodule

module CMP_5Bit (
  input  [4:0] A,
  input  [4:0] B,
  input  LT_in,
  input  EQ_in,
  input  GT_in,
  output LT,
  output EQ,
  output GT
);

  wire cmp_4bit_1_eq, cmp_4bit_1_gt, cmp_4bit_1_lt;

  CMP_4Bit cmp_4bit_1 (
    .A(A[3:0]), .B(B[3:0]), .LT_in(LT_in), .EQ_in(EQ_in), .GT_in(GT_in), .LT(cmp_4bit_1_lt),
    .EQ(cmp_4bit_1_eq), .GT(cmp_4bit_1_gt));
  CMP_1Bit cmp_1bit_1 (
    .A(A[4]), .B(B[4]), .LT_in(cmp_4bit_1_lt), .EQ_in(cmp_4bit_1_eq), .GT_in(cmp_4bit_1_gt), .LT(LT),
    .EQ(EQ), .GT(GT));
endmodule

module CMP_5Bit_Styled (
  input  [4:0] A,
  input  [4:0] B,
  output LT,
  output EQ,
  output GT
);

  CMP_5Bit cmp_5bit_1 (.A(A), .B(B), .EQ_in(1'b1), .LT(LT), .EQ(EQ), .GT(GT));  // open: LT_in, GT_in
endmodule

module RAM_WE_Styled (
  input  Clock,
  input  WE,
  input  Flag,
  input  Ins,
  output A,
  output B
);

  wire and_1_out, and_2_out, and_3_out, and_4_out, not_1_out, not_2_out, not_3_out, or_1_out, or_2_out;

  not not_1 (not_1_out, Clock);
  not not_2 (not_2_out, Flag);
  not not_3 (not_3_out, Ins);
  and and_1 (and_1_out, not_2_out, Ins);
  and and_2 (and_2_out, Flag, Ins);
  or or_1 (or_1_out, and_1_out, not_3_out);
  or or_2 (or_2_out, and_2_out, not_3_out);
  and and_3 (and_3_out, WE, or_1_out);
  and and_4 (and_4_out, WE, or_2_out);
  and and_5 (A, not_1_out, and_3_out);
  and and_6 (B, not_1_out, and_4_out);
endmodule

module Register_Selector (
  input  [4:0] N,
  input  OE,
  output Reg1,
  output Reg2,
  output Reg3,
  output Reg4,
  output Reg5,
  output Reg6,
  output Reg7,
  output Reg8
);

  Decoder_5Bit_Split decoder_5bit_split_1 (
    .A(N), .OE(OE), .B00001(Reg1), .B00010(Reg2), .B00011(Reg3), .B00100(Reg4), .B00101(Reg5), .B00110(Reg6),
    .B00111(Reg7), .B01000(Reg8));  // open: B00000, B01001, B01010, B01011, B01100, B01101, B01110, B01111, B10000, B10001, B10010, B10011, B10100, B10101, B10110, B10111, B11000, B11001, B11010, B11011, B11100, B11101, B11110, B11111
endmodule

module Reg_WE_Styled (
  input  WE,
  input  Sel,
  input  Ins,
  output out_4
);

  wire and_1_out, not_1_out, or_1_out;

  not not_1 (not_1_out, Ins);
  and and_1 (and_1_out, Sel, Ins);
  or or_1 (or_1_out, not_1_out, and_1_out);
  and and_2 (out_4, WE, or_1_out);
endmodule
